# Fritzing sketch BoatReceiver (saved by Fritzing 0.9.3b)

parts:
  920KV_Motor5 = DJI 920 KV Motor
  Part5 = Arduino Uno (Rev3) - ICSP
  Part6 = NRF24L01+ Breakout Board
  M5 = ESC
  920KV_Motor4 = DJI 920 KV Motor
  M4 = ESC
  J1 = Basic Servo

nets:
  N1: 920KV_Motor5.w, M5.W
  N2: 920KV_Motor5.v, M5.U
  N3: 920KV_Motor5.u, M5.V
  N4: Part5.D8, Part6.CS
  N5: Part5.D11_PWM/MOSI, Part6.MOSI
  N6: Part5.D12/MISO, Part6.MISO
  N7: Part5.D13/SCK, Part6.SCK
  GND: Part5.GND, Part6.GND, M4.GND, J1.gnd
  N8: Part5.D3_PWM, J1.pulse
  N9: Part5.D5_PWM, M4.DATA
  N10: Part5.D6_PWM, M5.DATA
  N11: Part5.D7, Part6.CE
  3V3: Part5.3V3, J1.vcc
  5V: Part5.5V, Part6.VCC
  N12: 920KV_Motor4.w, M4.W
  N13: 920KV_Motor4.v, M4.V
  N14: 920KV_Motor4.u, M4.U

notes:
  Counter Clockwise BLDC
  Clockweise BLDC

custom parts:
  DJI 920 KV Motor: DJI Brushless Outrunner 2212/920K Motor F330-550

// code stored in the sketch: WirelessBLDC.ino
#include <Servo.h>
#include <SPI.h>
#include <nRF24L01.h>
#include <RF24.h>

#define ESC1_PIN 5
#define ESC2_PIN 6

Servo esc1;
Servo esc2;
Servo fin;

const int Y_pin = 0;  // analog pin to Y output
const int X_pin = 1;  // analog pin to Y output

int motorSpeed1;
int motorSpeed2;

RF24 radio(9, 10); // CE, CSN

void setup() {
  Serial.begin(9600);


  fin.attach(3);
  for(int i=180;i>0;i--){
    fin.write(i);
    delay(10);
  }
  for(int i=0;i<180;i++){
    fin.write(i);
    delay(10);
  }

  pinMode(A0, INPUT);
  pinMode(A1, INPUT);

  esc1.attach(ESC1_PIN, 1000, 2000);
  esc1.write(180);
  delay(5000);
  esc1.write(0);
  delay(2000);
  esc1.write(10);  

  esc2.attach(ESC2_PIN, 1000, 2000);
  esc2.write(180);
  delay(5000);
  esc2.write(0);
  delay(2000);
  esc2.write(10);

  Serial.begin(9600);

  radio.begin();
  radio.openReadingPipe(1, 0xF0F0F0F0E1LL); // Set the pipe address to communicate between modules
  radio.startListening();

  pinMode(LED_BUILTIN, OUTPUT);
  digitalWrite(LED_BUILTIN, HIGH);
  delay(1000);
  digitalWrite(LED_BUILTIN, LOW);
}

void loop() {
  if (radio.available()) {
    int receivedData[2];
    radio.read(&receivedData, sizeof(receivedData));

    int ledYJoy = receivedData[0];
    int ledXJoy = receivedData[1];

    // motorSpeed1 = map(ledYJoy, 0, 1024, 0, 180);
    // motorSpeed2 = map(ledXJoy, 0, 1024, 180, 0);

    // Control the motors
    esc1.write(ledYJoy);
    esc2.write(ledYJoy);
    fin.write(ledXJoy);

    Serial.print(ledYJoy);
    Serial.print("  |  ");
    Serial.println(ledXJoy);
  }

  
  
}
