# Fritzing sketch RF nano (saved by Fritzing 0.9.3b)

parts:
  Part2 = Thumb Joystick
  Part3 = Thumb Joystick
  Part5 = Arduino Nano (Rev3.0) (ICSP)

nets:
  GND: Part2.GND, Part3.GND, Part5.GND
  N1: Part2.HORZ, Part5.A0
  VCC: Part2.VCC, Part3.VCC, Part5.3V3
  N2: Part3.HORZ, Part5.A1

notes:
  Transmitter

// code stored in the sketch: WirelessMotorControl.ino
#include <SPI.h>
#include <nRF24L01.h>
#include <RF24.h>


#define JoyStick_X_PIN A0
#define JoyStick_Y_PIN A1

RF24 radio(9, 10); // CE, CSN

int joyposVert;
int joyposHorz;

void setup() {
  Serial.begin(9600);

  pinMode(JoyStick_X_PIN, INPUT);
  pinMode(JoyStick_Y_PIN, INPUT);

  // lcd.begin(16, 2);
  // lcd.clear();
  // lcd.print("Hello, World!");
  // delay(1000);
  // lcd.clear();

  radio.begin();
  radio.openWritingPipe(0xF0F0F0F0E1LL); // Set the pipe address to communicate between modules
}

void loop() {
  int joyposVert = analogRead(JoyStick_X_PIN);
  int joyposHorz = analogRead(JoyStick_Y_PIN);

  int ledYJoy = map(joyposVert, 330, 0, 0, 180);
  int ledXJoy = map(joyposHorz, 1023, 0, 180, 0);

  Serial.print(ledYJoy);
  Serial.print("  |  ");
  Serial.println(ledXJoy);

  // lcd.setCursor(0, 0);
  // lcd.print("Throt Direc");
  // lcd.setCursor(0, 1);
  // lcd.print(" ");
  // lcd.print(ledYJoy);
  // lcd.setCursor(6, 1);
  // lcd.print(ledXJoy);
  // delay(50);
  // lcd.clear();

  int joystickData[2] = {ledYJoy, ledXJoy};

  // Send joystick data over NRF24L01+
  radio.write(&joystickData, sizeof(joystickData));

  delay(50); // Add a delay to avoid overwhelming the radio
}
