# Fritzing sketch WirelessMotorControl (saved by Fritzing 0.9.3b)
breadboards: 1

parts:
  Part1 = Arduino Uno (Rev3) - ICSP
  Part2 = Thumb Joystick
  Part3 = Thumb Joystick
  Part4 = NRF24L01+ Breakout Board

nets:
  N1: Part1.A0, Part2.HORZ
  N2: Part1.A1, Part3.VERT
  VCC: Part1.5V, Part2.VCC, Part3.VCC
  N3: Part1.ICSP_SCK, Part1.D13/SCK, Part4.SCK
  N4: Part1.ICSP_MOSI, Part1.D11_PWM/MOSI, Part4.MOSI
  GND: Part1.GND, Part2.GND, Part3.GND, Part4.GND
  N5: Part1.D9_PWM, Part4.CE
  N6: Part1.D10_PWM/SS, Part4.CS
  N7: Part1.D12/MISO, Part4.MISO
  3V3: Part1.3V3, Part4.VCC

notes:
  Transmitter

// code stored in the sketch: WirelessMotorControl.ino
#include <SPI.h>
#include <nRF24L01.h>
#include <RF24.h>


#define JoyStick_X_PIN A0
#define JoyStick_Y_PIN A1

RF24 radio(9, 10); // CE, CSN

int joyposVert;
int joyposHorz;

void setup() {
  Serial.begin(9600);

  pinMode(JoyStick_X_PIN, INPUT);
  pinMode(JoyStick_Y_PIN, INPUT);

  // lcd.begin(16, 2);
  // lcd.clear();
  // lcd.print("Hello, World!");
  // delay(1000);
  // lcd.clear();

  radio.begin();
  radio.openWritingPipe(0xF0F0F0F0E1LL); // Set the pipe address to communicate between modules
}

void loop() {
  int joyposVert = analogRead(JoyStick_X_PIN);
  int joyposHorz = analogRead(JoyStick_Y_PIN);

  int ledYJoy = map(joyposVert, 330, 0, 0, 180);
  int ledXJoy = map(joyposHorz, 1023, 0, 180, 0);

  Serial.print(ledYJoy);
  Serial.print("  |  ");
  Serial.println(ledXJoy);

  // lcd.setCursor(0, 0);
  // lcd.print("Throt Direc");
  // lcd.setCursor(0, 1);
  // lcd.print(" ");
  // lcd.print(ledYJoy);
  // lcd.setCursor(6, 1);
  // lcd.print(ledXJoy);
  // delay(50);
  // lcd.clear();

  int joystickData[2] = {ledYJoy, ledXJoy};

  // Send joystick data over NRF24L01+
  radio.write(&joystickData, sizeof(joystickData));

  delay(50); // Add a delay to avoid overwhelming the radio
}
